# Fritzing sketch elektriskeem (saved by Fritzing 1.0.6)

parts:
  Mod1 = Amica NodeMCU DEVKIT 1.0
  LED1 = smd LED [color="Red (633nm)" package="1206 [SMD]"]  # not connected
  LED2 = smd LED [color="Yellow (595nm)" package="1206 [SMD]"]  # not connected
  LED3 = smd LED [color="Green (555nm)" package="1206 [SMD]"]  # not connected
  LED4 = smd LED [color="Green (555nm)" package="1206 [SMD]"]  # not connected
  LED5 = smd LED [color="Red (660nm)" package="1206 [SMD]"]  # not connected
  LED6 = smd LED [color="Green (555nm)" package="1206 [SMD]"]
  R1 = Resistor [tolerance=±5% resistance=220 package="0402 [SMD]"]
  R2 = Resistor [tolerance=±5% resistance=220 package="0402 [SMD]"]
  R3 = Resistor [tolerance=±5% resistance=220 package="0402 [SMD]"]
  R4 = Resistor [tolerance=±5% resistance=220 package="0402 [SMD]"]
  R5 = Resistor [tolerance=±5% resistance=220 package="0402 [SMD]"]
  R6 = Resistor [tolerance=±5% resistance=220 package="0402 [SMD]"]

nets:
  N1: Mod1.pin5, R1.Pin_0
  N2: Mod1.pin6, R6.Pin_0
  N3: Mod1.pin8, R4.Pin_0
  N4: Mod1.pin_9, Mod1.pin_25, LED6.cathode
  N5: Mod1.pin_13, R5.Pin_0
  N6: Mod1.pin_14, R3.Pin_0
  N7: Mod1.pin_15, R2.Pin_0
